# Fritzing sketch Circuit (saved by Fritzing 0.9.3b)

parts:
  Part1 = Arduino Nano (Rev3.0) (ICSP)
  HC-SR04_Sensor_1 = HC-SR04 Ultrasonic Distance Sensor
  HC-SR04_Sensor_2 = HC-SR04 Ultrasonic Distance Sensor
  HC-SR04_Sensor_3 = HC-SR04 Ultrasonic Distance Sensor
  S1 = H-Bridge with L298N
  M1 = DC Motor
  M2 = DC Motor
  M3 = DC Motor
  M4 = DC Motor
  U1 = LIPO-2000mAh [package=lipo-2000]
  Part3 = Bluetooth HC-05 Macho

nets:
  N1: Part1.D1/TX, Part3.RXD
  N2: Part1.D0/RX, Part3.TXD
  GND: Part1.GND, HC-SR04_Sensor_1.GND, HC-SR04_Sensor_2.GND, HC-SR04_Sensor_3.GND, S1.GND, U1.-, Part3.GND
  N3: Part1.D2, HC-SR04_Sensor_2.ECHO
  N4: Part1.D3, HC-SR04_Sensor_2.TRIG
  N5: Part1.D4, S1.IN4
  N6: Part1.D5, S1.IN3
  N7: Part1.D6, S1.ENA, S1.ENB
  N8: Part1.D7, S1.IN2
  N9: Part1.D8, S1.IN1
  N10: Part1.D9, HC-SR04_Sensor_3.ECHO
  N11: Part1.D10, HC-SR04_Sensor_3.TRIG
  N12: Part1.D11/MOSI, HC-SR04_Sensor_1.ECHO
  N13: Part1.D12/MISO, HC-SR04_Sensor_1.TRIG
  VIN: Part1.VIN, S1.5V
  VCC: Part1.3V3, HC-SR04_Sensor_1.VCC, HC-SR04_Sensor_2.VCC, HC-SR04_Sensor_3.VCC, Part3.VCC
  N14: S1.12V, U1.+
  N15: S1.M1-01, M1.pin_2, M2.pin_2
  N16: S1.M1-02, M1.pin_1, M2.pin_1
  N17: S1.M2-01, M3.pin_2, M4.pin_2
  N18: S1.M2-02, M3.pin_1, M4.pin_1

notes:
  Right
  left
  middle

custom parts:
  H-Bridge with L298N: h-bridge
